# Fritzing sketch circuit (saved by Fritzing 0.9.2b)
breadboards: 1

parts:
  Part1 = Arduino Uno (Rev3)
  R1 = PHOTOCELL [package=photocell]
  R2 = Resistor [tolerance=±5% resistance=220 package=THT]
  LED1 = LED - 5mm [color="Red (633nm)" package="5 mm [THT]"]

nets:
  N1: Part1.A2, R1.P$1, R2.Pin_1
  N2: Part1.D13/SCK, LED1.anode
  N3: Part1.GND, R1.P$2, LED1.cathode
  N4: Part1.5V, R2.Pin_0
